// Logisim project portas_logicas.circ as structural Verilog: 1 circuit, main circuit main
// d
module main (
  input  a,
  input  b,
  input  in_3,
  input  c,
  input  in_5,
  input  in_6,
  input  d,
  input  in_8,
  input  e,
  input  in_10,
  input  in_11,
  input  in_12,
  input  in_13,
  input  in_14,
  input  in_15,
  input  in_16,
  input  in_17,
  input  in_18,
  input  in_19,
  input  in_20,
  input  in_21,
  input  in_22,
  input  in_23,
  input  in_24,
  input  a_2,
  input  in_26,
  input  b_2,
  input  in_28,
  input  b_3,
  input  d_2,
  input  e_2,
  input  f,
  input  in_33,
  input  in_34,
  input  in_35,
  input  in_36,
  input  in_37,
  input  in_38,
  input  in_39,
  input  in_40,
  input  in_41,
  input  in_42,
  input  in_43,
  input  in_44,
  input  in_45,
  input  in_46,
  input  in_47,
  input  in_48,
  input  in_49,
  output S,
  output S_2,
  output out_52,
  output C_2,
  output c_3,
  output S_3
);

  wire AND_2_out, AND_3_out, AND_4_out, AND_5_out, AND_8_out, and_9_out, and_25_out, AND_out, OR_2_out,
       OR_3_out, OR_4_out, OR_5_out, OR_out, undriven, undriven_2, undriven_3, undriven_4, undriven_5,
       undriven_6, undriven_7, undriven_8, undriven_9, undriven_10, undriven_11, undriven_12, undriven_13,
       undriven_14, undriven_15, undriven_16, undriven_17, undriven_18, undriven_19, undriven_20, undriven_21;

  buf AND (AND_out, in_40);  // AND_Gate
  and AND_2 (AND_2_out, a, b, b);
  and AND_3 (AND_3_out, d, e);
  buf OR (OR_out, in_15);  // OR_Gate
  or OR_2 (OR_2_out, in_19, in_21);
  and AND_4 (AND_4_out, a_2, b_2);
  or OR_3 (OR_3_out, b_3, d_2);
  or OR_4 (OR_4_out, e_2, f);
  or OR_5 (OR_5_out, in_36, in_38);
  and AND_5 (AND_5_out, in_43, in_45);
  and AND_6 (S, AND_2_out, AND_3_out);
  nand AND_7 (out_52, OR_out, OR_2_out);
  or OR_6 (C_2, AND_4_out, OR_3_out, OR_4_out);
  and AND_8 (AND_8_out, OR_5_out, AND_out);
  or OR_7 (c_3, AND_8_out, AND_5_out);
  and and_9 (and_9_out, in_3, undriven);
  and and_10 (and_9_out, undriven, in_5, undriven_2);
  and and_11 (and_9_out, undriven_2, in_6, undriven_3);
  and and_12 (and_9_out, undriven_3, in_8);
  and and_13 (and_9_out, in_10, undriven_4);
  and and_14 (and_9_out, undriven_4, in_11, undriven_5);
  and and_15 (and_9_out, undriven_5, in_12, undriven_6);
  and and_16 (and_9_out, undriven_6, in_13);
  and and_17 (and_9_out, in_16, undriven_7);
  and and_18 (and_9_out, undriven_7, in_18, undriven_8);
  and and_19 (and_9_out, undriven_8, in_20, undriven_9);
  and and_20 (and_9_out, undriven_9, in_22);
  and and_21 (and_9_out, in_23, in_23, undriven_10);
  and and_22 (and_9_out, undriven_10, in_24, undriven_11);
  and and_23 (and_9_out, undriven_11, in_26, undriven_12);
  and and_24 (and_9_out, undriven_12, in_28);
  and and_25 (and_25_out, in_33, undriven_13);
  and and_26 (and_25_out, undriven_13, in_34, undriven_14);
  and and_27 (and_25_out, undriven_14, in_35, undriven_15);
  and and_28 (and_25_out, undriven_15, in_37);
  and and_29 (and_25_out, in_39, undriven_16);
  and and_30 (and_25_out, undriven_16, in_41, undriven_17);
  and and_31 (and_25_out, undriven_17, in_42, undriven_18);
  and and_32 (and_25_out, undriven_18, in_44);
  and and_33 (and_25_out, in_46, undriven_19);
  and and_34 (and_25_out, undriven_19, in_47, undriven_20);
  and and_35 (and_25_out, undriven_20, in_48, undriven_21);
  and and_36 (and_25_out, undriven_21, in_49);
  and AND_37 (S_2, and_9_out, and_9_out, and_9_out, and_9_out, and_9_out, and_9_out, and_9_out, and_9_out, and_9_out, and_9_out, and_9_out, and_9_out, and_9_out, and_9_out, and_9_out);
  and AND_38 (S_3, and_25_out, and_25_out, and_25_out, and_25_out, and_25_out, and_25_out, and_25_out, and_25_out, and_25_out, and_25_out, and_25_out, and_25_out);

  // Notes on the sheet:
  //   Exercicio 2
  //   Exercicio 1
  //   Exercicio 3
  //   Exercicio 4
  //   Exercicio 5
  //   Exercicio 6
  //   145
endmodule
